# Fritzing sketch EnergyFrame (saved by Fritzing 0.9.9b)

parts:
  A1 = Wemos S2 Mini [part_number="WeMos D1 Mini Lite"]
  Part1 = 0.56" 7-segment LED Backpack [part_number=881]
  Part2 = 0.56" 7-segment LED Backpack [part_number=879]
  S1 = Round Pushbutton
  S2 = Round Pushbutton
  meter1 = meter
  meter2 = meter

nets:
  VDD: A1.Pin_17, Part1.VDD, Part2.VDD
  GND: A1.Pin_18, A1.Pin_26, Part1.GND, Part2.GND, S1.leg0, S2.leg0, meter1.Com, meter2.Com
  N1: A1.Pin_19, S2.leg1
  N2: A1.Pin_20, S1.leg1
  N3: A1.Pin_21, meter1.Positive
  N4: A1.Pin_22, meter2.Positive
  N5: A1.Pin_23, Part1.SDA, Part2.SDA
  N6: A1.Pin_24, Part1.SCL, Part2.SCL

custom parts:
  Wemos S2 Mini: A mini wifi board based on the ESP32-S2FN4R2.
  0.56" 7-segment LED Backpack: This 0.56" 7-segment LED display includes a driver chip for simple control via an I2C interface. The backpack features address-selection jumpers so you can connect up to eight displays on a single I2C bus.
  0.56" 7-segment LED Backpack: This 0.56" 7-segment LED display includes a driver chip for simple control via an I2C interface. The backpack features address-selection jumpers so you can connect up to eight displays on a single I2C bus.
  meter: A generic analog meter.
